// Digital circuit xoxo.dig as structural Verilog
module xoxo (
  input  clk,
  output out_2
);

  wire and_1_out, and_2_out, and_3_out, and_7_out, and_8_out, and_9_out, and_14_out, and_15_out, BA, BB, BC,
       BD, BE, BF, BG, BH, BI, CBA, CBB, CBC, CBD, CBE, CBF, CBG, CBH, CBI, CFA, CFB, CFC, CFD, CFE, CFF,
       CFG, CFH, CFI, CLA, delay_1_out, delay_2_out, delay_3_out, delay_4_out, delay_5_out, delay_6_out,
       delay_7_out, delay_8_out, delay_9_out, delay_10_out, delay_11_out, delay_12_out, delay_13_out,
       delay_14_out, delay_15_out, delay_16_out, delay_17_out, delay_18_out, delay_19_out, delay_20_out,
       delay_21_out, delay_22_out, delay_23_out, delay_24_out, delay_25_out, delay_26_out, delay_27_out,
       delay_28_out, delay_29_out, delay_30_out, delay_31_out, delay_32_out, delay_33_out, delay_34_out,
       delay_35_out, delay_36_out, delay_37_out, delay_38_out, delay_39_out, delay_40_out, delay_41_out,
       delay_42_out, delay_43_out, delay_44_out, delay_45_out, delay_46_out, delay_47_out, delay_48_out,
       delay_49_out, delay_50_out, delay_51_out, delay_52_out, demultiplexer_1_out_0, demultiplexer_1_out_1,
       lookuptable_1_out, lookuptable_2_out, lookuptable_3_out, lookuptable_4_out, lookuptable_5_out,
       lookuptable_6_out, lookuptable_7_out, lookuptable_8_out, monoflop_1_q, monoflop_2_q, monoflop_3_q,
       monoflop_4_q, monoflop_5_q, monoflop_6_q, monoflop_7_q, monoflop_8_q, monoflop_9_q, not_1_out,
       not_2_out, not_3_out, not_4_out, not_5_out, not_6_out, not_7_out, not_8_out, not_9_out, not_10_out,
       or_1_out, t_ff_1_q, TUN, WS;
  wire [3:0] priorityencoder_1_num;
  wire [15:0] A, B, C, CSA, CSB, CSC, CSD, CSE, CSF, CSG, CSH, CSI, D, E, F, G, H, I, multiplexer_1_out, SA,
       SB, SC, SD, SE, SF, SG, SH, SI;

  Delay delay_1 (.in(WS), .out(delay_1_out));
  Monoflop #(.timerDelay(3)) monoflop_1 (.C(delay_1_out), .R(1'b0), .Q(monoflop_1_q));  // open: nQ
  Delay #(.delayTime(4)) delay_2 (.in(CFA), .out(delay_2_out));
  Delay #(.delayTime(4)) delay_3 (.in(CFE), .out(delay_3_out));
  Delay #(.delayTime(4)) delay_4 (.in(CFI), .out(delay_4_out));
  Delay #(.delayTime(4)) delay_5 (.in(CFA), .out(delay_5_out));
  Delay #(.delayTime(4)) delay_6 (.in(CFD), .out(delay_6_out));
  Delay #(.delayTime(4)) delay_7 (.in(CFG), .out(delay_7_out));
  Delay #(.delayTime(4)) delay_8 (.in(CFA), .out(delay_8_out));
  Delay #(.delayTime(4)) delay_9 (.in(CFB), .out(delay_9_out));
  Delay #(.delayTime(4)) delay_10 (.in(CFC), .out(delay_10_out));
  Demultiplexer demultiplexer_1 (
    .sel(not_1_out), .in(monoflop_1_q), .out_0(demultiplexer_1_out_0), .out_1(demultiplexer_1_out_1));
  not not_1 (not_1_out, TUN);
  PullDown pulldown_1 (.out(TUN));
  and and_1 (and_1_out, CSI[0], CSE[0], CSA[0]);
  LookUpTable lookuptable_1 (.in0(CSA[0]), .in1(CSE[0]), .in2(CSI[0]), .out(lookuptable_1_out));
  and and_2 (and_2_out, CSG[0], CSD[0], CSA[0]);
  LookUpTable lookuptable_2 (.in0(CSA[0]), .in1(CSD[0]), .in2(CSG[0]), .out(lookuptable_2_out));
  and and_3 (and_3_out, CSC[0], CSB[0], CSA[0]);
  LookUpTable lookuptable_3 (.in0(CSA[0]), .in1(CSB[0]), .in2(CSC[0]), .out(lookuptable_3_out));
  Monoflop #(.timerDelay(4)) monoflop_2 (.C(and_1_out), .R(1'b0), .Q(monoflop_2_q));  // open: nQ
  and and_4 (WS, lookuptable_1_out, delay_2_out, delay_3_out, delay_4_out);
  Monoflop #(.timerDelay(4)) monoflop_3 (.C(and_2_out), .R(1'b0), .Q(monoflop_3_q));  // open: nQ
  and and_5 (WS, lookuptable_2_out, delay_5_out, delay_6_out, delay_7_out);
  Monoflop #(.timerDelay(4)) monoflop_4 (.C(and_3_out), .R(1'b0), .Q(monoflop_4_q));  // open: nQ
  and and_6 (WS, lookuptable_3_out, delay_8_out, delay_9_out, delay_10_out);
  assign A = demultiplexer_1_out_0 ? 16'hc3 : 16'bz;  // Driver driver_1
  assign A = demultiplexer_1_out_1 ? 16'h2400 : 16'bz;  // Driver driver_2
  PullDown #(.Bits(16)) pulldown_2 (.out(A));
  PullDown #(.Bits(16)) pulldown_3 (.out(A));
  DiodeForward diodeforward_1 (.in(monoflop_2_q), .out(TUN));
  DiodeForward diodeforward_2 (.in(WS), .out(CLA));
  DiodeForward diodeforward_3 (.in(WS), .out(CLA));
  DiodeForward diodeforward_4 (.in(WS), .out(CLA));
  DiodeForward diodeforward_5 (.in(WS), .out(CLA));
  DiodeForward diodeforward_6 (.in(WS), .out(CLA));
  DiodeForward diodeforward_7 (.in(WS), .out(CLA));
  DiodeForward diodeforward_8 (.in(WS), .out(CLA));
  DiodeForward diodeforward_9 (.in(WS), .out(CLA));
  DiodeForward diodeforward_10 (.in(WS), .out(CLA));
  DiodeForward diodeforward_11 (.in(monoflop_3_q), .out(TUN));
  DiodeForward diodeforward_12 (.in(WS), .out(CLA));
  DiodeForward diodeforward_13 (.in(WS), .out(CLA));
  DiodeForward diodeforward_14 (.in(WS), .out(CLA));
  DiodeForward diodeforward_15 (.in(WS), .out(CLA));
  DiodeForward diodeforward_16 (.in(WS), .out(CLA));
  DiodeForward diodeforward_17 (.in(WS), .out(CLA));
  DiodeForward diodeforward_18 (.in(WS), .out(CLA));
  DiodeForward diodeforward_19 (.in(WS), .out(CLA));
  DiodeForward diodeforward_20 (.in(WS), .out(CLA));
  DiodeForward diodeforward_21 (.in(monoflop_4_q), .out(TUN));
  DiodeForward diodeforward_22 (.in(WS), .out(CLA));
  DiodeForward diodeforward_23 (.in(WS), .out(CLA));
  DiodeForward diodeforward_24 (.in(WS), .out(CLA));
  DiodeForward diodeforward_25 (.in(WS), .out(CLA));
  DiodeForward diodeforward_26 (.in(WS), .out(CLA));
  DiodeForward diodeforward_27 (.in(WS), .out(CLA));
  DiodeForward diodeforward_28 (.in(WS), .out(CLA));
  DiodeForward diodeforward_29 (.in(WS), .out(CLA));
  DiodeForward diodeforward_30 (.in(WS), .out(CLA));
  assign B = demultiplexer_1_out_0 ? 16'h3 : 16'bz;  // Driver driver_3
  PullDown #(.Bits(16)) pulldown_4 (.out(B));
  assign C = demultiplexer_1_out_1 ? 16'h9000 : 16'bz;  // Driver driver_4
  Delay #(.delayTime(4)) delay_11 (.in(CFC), .out(delay_11_out));
  Delay #(.delayTime(4)) delay_12 (.in(CFE), .out(delay_12_out));
  Delay #(.delayTime(4)) delay_13 (.in(CFG), .out(delay_13_out));
  Delay #(.delayTime(4)) delay_14 (.in(CFB), .out(delay_14_out));
  Delay #(.delayTime(4)) delay_15 (.in(CFE), .out(delay_15_out));
  Delay #(.delayTime(4)) delay_16 (.in(CFH), .out(delay_16_out));
  Delay #(.delayTime(4)) delay_17 (.in(CFD), .out(delay_17_out));
  Delay #(.delayTime(4)) delay_18 (.in(CFE), .out(delay_18_out));
  Delay #(.delayTime(4)) delay_19 (.in(CFF), .out(delay_19_out));
  assign C = demultiplexer_1_out_0 ? 16'hf : 16'bz;  // Driver driver_5
  PullDown #(.Bits(16)) pulldown_5 (.out(C));
  PullDown #(.Bits(16)) pulldown_6 (.out(C));
  and and_7 (and_7_out, CSG[0], CSE[0], CSC[0]);
  LookUpTable lookuptable_4 (.in0(CSC[0]), .in1(CSE[0]), .in2(CSG[0]), .out(lookuptable_4_out));
  and and_8 (and_8_out, CSH[0], CSE[0], CSB[0]);
  LookUpTable lookuptable_5 (.in0(CSB[0]), .in1(CSE[0]), .in2(CSH[0]), .out(lookuptable_5_out));
  and and_9 (and_9_out, CSF[0], CSE[0], CSD[0]);
  LookUpTable lookuptable_6 (.in0(CSD[0]), .in1(CSE[0]), .in2(CSF[0]), .out(lookuptable_6_out));
  assign D = demultiplexer_1_out_0 ? 16'hc0 : 16'bz;  // Driver driver_6
  assign E = demultiplexer_1_out_1 ? 16'hb400 : 16'bz;  // Driver driver_7
  PullDown #(.Bits(16)) pulldown_7 (.out(E));
  Monoflop #(.timerDelay(4)) monoflop_5 (.C(and_7_out), .R(1'b0), .Q(monoflop_5_q));  // open: nQ
  and and_10 (WS, lookuptable_4_out, delay_11_out, delay_12_out, delay_13_out);
  Monoflop #(.timerDelay(4)) monoflop_6 (.C(and_8_out), .R(1'b0), .Q(monoflop_6_q));  // open: nQ
  and and_11 (WS, lookuptable_5_out, delay_14_out, delay_15_out, delay_16_out);
  Monoflop #(.timerDelay(4)) monoflop_7 (.C(and_9_out), .R(1'b0), .Q(monoflop_7_q));  // open: nQ
  and and_12 (WS, lookuptable_6_out, delay_17_out, delay_18_out, delay_19_out);
  PullDown #(.Bits(16)) pulldown_8 (.out(D));
  assign F = demultiplexer_1_out_0 ? 16'hc : 16'bz;  // Driver driver_8
  DiodeForward diodeforward_31 (.in(monoflop_5_q), .out(TUN));
  DiodeForward diodeforward_32 (.in(WS), .out(CLA));
  DiodeForward diodeforward_33 (.in(WS), .out(CLA));
  DiodeForward diodeforward_34 (.in(WS), .out(CLA));
  DiodeForward diodeforward_35 (.in(WS), .out(CLA));
  DiodeForward diodeforward_36 (.in(WS), .out(CLA));
  DiodeForward diodeforward_37 (.in(WS), .out(CLA));
  DiodeForward diodeforward_38 (.in(WS), .out(CLA));
  DiodeForward diodeforward_39 (.in(WS), .out(CLA));
  DiodeForward diodeforward_40 (.in(WS), .out(CLA));
  DiodeForward diodeforward_41 (.in(monoflop_6_q), .out(TUN));
  DiodeForward diodeforward_42 (.in(WS), .out(CLA));
  DiodeForward diodeforward_43 (.in(WS), .out(CLA));
  DiodeForward diodeforward_44 (.in(WS), .out(CLA));
  DiodeForward diodeforward_45 (.in(WS), .out(CLA));
  DiodeForward diodeforward_46 (.in(WS), .out(CLA));
  DiodeForward diodeforward_47 (.in(WS), .out(CLA));
  DiodeForward diodeforward_48 (.in(WS), .out(CLA));
  DiodeForward diodeforward_49 (.in(WS), .out(CLA));
  DiodeForward diodeforward_50 (.in(WS), .out(CLA));
  DiodeForward diodeforward_51 (.in(monoflop_7_q), .out(TUN));
  DiodeForward diodeforward_52 (.in(WS), .out(CLA));
  DiodeForward diodeforward_53 (.in(WS), .out(CLA));
  DiodeForward diodeforward_54 (.in(WS), .out(CLA));
  DiodeForward diodeforward_55 (.in(WS), .out(CLA));
  DiodeForward diodeforward_56 (.in(WS), .out(CLA));
  DiodeForward diodeforward_57 (.in(WS), .out(CLA));
  DiodeForward diodeforward_58 (.in(WS), .out(CLA));
  DiodeForward diodeforward_59 (.in(WS), .out(CLA));
  DiodeForward diodeforward_60 (.in(WS), .out(CLA));
  PullDown #(.Bits(16)) pulldown_9 (.out(F));
  assign G = demultiplexer_1_out_1 ? 16'h9000 : 16'bz;  // Driver driver_9
  PullDown #(.Bits(16)) pulldown_10 (.out(G));
  Delay #(.delayTime(4)) delay_20 (.in(CFC), .out(delay_20_out));
  Delay #(.delayTime(4)) delay_21 (.in(CFF), .out(delay_21_out));
  Delay #(.delayTime(4)) delay_22 (.in(CFI), .out(delay_22_out));
  Delay #(.delayTime(4)) delay_23 (.in(CFG), .out(delay_23_out));
  Delay #(.delayTime(4)) delay_24 (.in(CFH), .out(delay_24_out));
  Delay #(.delayTime(4)) delay_25 (.in(CFI), .out(delay_25_out));
  assign G = demultiplexer_1_out_0 ? 16'hf0 : 16'bz;  // Driver driver_10
  PullDown #(.Bits(16)) pulldown_11 (.out(G));
  and and_13 (CLA, CFA, CFB, CFC, CFD, CFE, CFF, CFG, CFH, CFI);
  and and_14 (and_14_out, CSI[0], CSF[0], CSC[0]);
  LookUpTable lookuptable_7 (.in0(CSC[0]), .in1(CSF[0]), .in2(CSI[0]), .out(lookuptable_7_out));
  and and_15 (and_15_out, CSI[0], CSH[0], CSG[0]);
  LookUpTable lookuptable_8 (.in0(CSG[0]), .in1(CSH[0]), .in2(CSI[0]), .out(lookuptable_8_out));
  assign I = demultiplexer_1_out_1 ? 16'h2400 : 16'bz;  // Driver driver_11
  PullDown #(.Bits(16)) pulldown_12 (.out(I));
  assign H = demultiplexer_1_out_0 ? 16'h30 : 16'bz;  // Driver driver_12
  Monoflop #(.timerDelay(4)) monoflop_8 (.C(and_14_out), .R(1'b0), .Q(monoflop_8_q));  // open: nQ
  and and_16 (WS, lookuptable_7_out, delay_20_out, delay_21_out, delay_22_out);
  Monoflop #(.timerDelay(4)) monoflop_9 (.C(and_15_out), .R(1'b0), .Q(monoflop_9_q));  // open: nQ
  and and_17 (WS, lookuptable_8_out, delay_23_out, delay_24_out, delay_25_out);
  PullDown #(.Bits(16)) pulldown_13 (.out(H));
  DiodeForward diodeforward_61 (.in(monoflop_8_q), .out(TUN));
  DiodeForward diodeforward_62 (.in(WS), .out(CLA));
  DiodeForward diodeforward_63 (.in(WS), .out(CLA));
  DiodeForward diodeforward_64 (.in(WS), .out(CLA));
  DiodeForward diodeforward_65 (.in(WS), .out(CLA));
  DiodeForward diodeforward_66 (.in(WS), .out(CLA));
  DiodeForward diodeforward_67 (.in(WS), .out(CLA));
  DiodeForward diodeforward_68 (.in(WS), .out(CLA));
  DiodeForward diodeforward_69 (.in(WS), .out(CLA));
  DiodeForward diodeforward_70 (.in(WS), .out(CLA));
  DiodeForward diodeforward_71 (.in(monoflop_9_q), .out(TUN));
  DiodeForward diodeforward_72 (.in(WS), .out(CLA));
  DiodeForward diodeforward_73 (.in(WS), .out(CLA));
  DiodeForward diodeforward_74 (.in(WS), .out(CLA));
  DiodeForward diodeforward_75 (.in(WS), .out(CLA));
  DiodeForward diodeforward_76 (.in(WS), .out(CLA));
  DiodeForward diodeforward_77 (.in(WS), .out(CLA));
  DiodeForward diodeforward_78 (.in(WS), .out(CLA));
  DiodeForward diodeforward_79 (.in(WS), .out(CLA));
  DiodeForward diodeforward_80 (.in(WS), .out(CLA));
  assign I = demultiplexer_1_out_0 ? 16'h3c : 16'bz;  // Driver driver_13
  PullDown #(.Bits(16)) pulldown_14 (.out(I));
  assign CBA = not_2_out ? BA : 1'bz;  // Driver driver_14
  assign CBD = not_3_out ? BD : 1'bz;  // Driver driver_15
  assign CBG = not_4_out ? BG : 1'bz;  // Driver driver_16
  Delay #(.delayTime(2)) delay_26 (.in(CBA), .out(delay_26_out));
  Delay #(.delayTime(5)) delay_27 (.in(CLA), .out(delay_27_out));
  Delay #(.delayTime(2)) delay_28 (.in(CBD), .out(delay_28_out));
  Delay #(.delayTime(5)) delay_29 (.in(CLA), .out(delay_29_out));
  Delay #(.delayTime(2)) delay_30 (.in(CBG), .out(delay_30_out));
  Delay #(.delayTime(5)) delay_31 (.in(CLA), .out(delay_31_out));
  PullDown pulldown_15 (.out(CBC));
  PullDown pulldown_16 (.out(CBB));
  PullDown pulldown_17 (.out(CBA));
  D_FF_AS d_ff_as_1 (.Set(1'b0), .D(1'b1), .C(BA), .Clr(CLA), .Q(CFA));  // open: nQ
  PullDown pulldown_18 (.out(CLA));
  not not_2 (not_2_out, delay_32_out);
  D_FF_AS #(.Bits(16)) d_ff_as_2 (.Set(1'b0), .D(SA), .C(delay_26_out), .Clr(delay_27_out), .Q(CSA));  // open: nQ
  PullDown pulldown_19 (.out(delay_27_out));
  D_FF_AS d_ff_as_3 (.Set(1'b0), .D(1'b1), .C(BD), .Clr(CLA), .Q(CFD));  // open: nQ
  PullDown pulldown_20 (.out(CLA));
  not not_3 (not_3_out, delay_33_out);
  D_FF_AS #(.Bits(16)) d_ff_as_4 (.Set(1'b0), .D(SD), .C(delay_28_out), .Clr(delay_29_out), .Q(CSD));  // open: nQ
  PullDown pulldown_21 (.out(delay_29_out));
  D_FF_AS d_ff_as_5 (.Set(1'b0), .D(1'b1), .C(BG), .Clr(CLA), .Q(CFG));  // open: nQ
  PullDown pulldown_22 (.out(CLA));
  not not_4 (not_4_out, delay_34_out);
  D_FF_AS #(.Bits(16)) d_ff_as_6 (.Set(1'b0), .D(SG), .C(delay_30_out), .Clr(delay_31_out), .Q(CSG));  // open: nQ
  PullDown pulldown_23 (.out(delay_31_out));
  PullDown pulldown_24 (.out(CBG));
  PullDown pulldown_25 (.out(CBF));
  PullDown pulldown_26 (.out(CBE));
  PullDown pulldown_27 (.out(CBD));
  Delay delay_32 (.in(CFA), .out(delay_32_out));
  Delay delay_33 (.in(CFD), .out(delay_33_out));
  Delay delay_34 (.in(CFG), .out(delay_34_out));
  or or_1 (or_1_out, CBA, CBB, CBC, CBD, CBE, CBF, CBG, CBH, CBI);
  PullDown pulldown_28 (.out(CBI));
  PullDown pulldown_29 (.out(CBH));
  assign A = CFA ? CSA : 16'bz;  // Driver driver_17
  PullDown #(.Bits(16)) pulldown_30 (.out(A));
  assign D = CFD ? CSD : 16'bz;  // Driver driver_18
  PullDown #(.Bits(16)) pulldown_31 (.out(D));
  assign G = CFG ? CSG : 16'bz;  // Driver driver_19
  PullDown #(.Bits(16)) pulldown_32 (.out(G));
  assign CBB = not_5_out ? BB : 1'bz;  // Driver driver_20
  assign CBE = not_6_out ? BE : 1'bz;  // Driver driver_21
  assign CBH = not_7_out ? BH : 1'bz;  // Driver driver_22
  T_FF t_ff_1 (.T(1'b1), .C(or_1_out), .Q(t_ff_1_q));  // open: nQ
  PullDown pulldown_33 (.out(CLA));
  not not_5 (not_5_out, delay_41_out);
  Delay #(.delayTime(2)) delay_35 (.in(CBB), .out(delay_35_out));
  Delay #(.delayTime(5)) delay_36 (.in(CLA), .out(delay_36_out));
  PullDown pulldown_34 (.out(delay_36_out));
  PullDown pulldown_35 (.out(CLA));
  not not_6 (not_6_out, delay_42_out);
  Delay #(.delayTime(2)) delay_37 (.in(CBE), .out(delay_37_out));
  Delay #(.delayTime(5)) delay_38 (.in(CLA), .out(delay_38_out));
  PullDown pulldown_36 (.out(delay_38_out));
  PullDown pulldown_37 (.out(CLA));
  not not_7 (not_7_out, delay_43_out);
  Delay #(.delayTime(2)) delay_39 (.in(CBH), .out(delay_39_out));
  Delay #(.delayTime(5)) delay_40 (.in(CLA), .out(delay_40_out));
  PullDown pulldown_38 (.out(delay_40_out));
  PriorityEncoder #(.Selector_Bits(4)) priorityencoder_1 (
    .in0(1'b0), .in1(BA), .in2(BB), .in3(BC), .in4(BD), .in5(BE), .in6(BF), .in7(BG), .in8(BH), .in9(BI),
    .in10(1'b0), .in11(1'b0), .in12(1'b0), .in13(1'b0), .in14(1'b0), .in15(1'b0), .num(priorityencoder_1_num));  // open: any
  Multiplexer #(.Bits(16)) multiplexer_1 (.sel(t_ff_1_q), .in_0(16'hb400), .in_1(16'hff), .out(multiplexer_1_out));
  D_FF_AS d_ff_as_7 (.Set(1'b0), .D(1'b1), .C(BB), .Clr(CLA), .Q(CFB));  // open: nQ
  Delay delay_41 (.in(CFB), .out(delay_41_out));
  D_FF_AS #(.Bits(16)) d_ff_as_8 (.Set(1'b0), .D(SB), .C(delay_35_out), .Clr(delay_36_out), .Q(CSB));  // open: nQ
  D_FF_AS d_ff_as_9 (.Set(1'b0), .D(1'b1), .C(BE), .Clr(CLA), .Q(CFE));  // open: nQ
  Delay delay_42 (.in(CFE), .out(delay_42_out));
  D_FF_AS #(.Bits(16)) d_ff_as_10 (.Set(1'b0), .D(SE), .C(delay_37_out), .Clr(delay_38_out), .Q(CSE));  // open: nQ
  D_FF_AS d_ff_as_11 (.Set(1'b0), .D(1'b1), .C(BH), .Clr(CLA), .Q(CFH));  // open: nQ
  Delay delay_43 (.in(CFH), .out(delay_43_out));
  D_FF_AS #(.Bits(16)) d_ff_as_12 (.Set(1'b0), .D(SH), .C(delay_39_out), .Clr(delay_40_out), .Q(CSH));  // open: nQ
  Demultiplexer #(.Selector_Bits(4), .Bits(16)) demultiplexer_2 (
    .sel(priorityencoder_1_num), .in(multiplexer_1_out), .out_1(SA), .out_2(SB), .out_3(SC), .out_4(SD),
    .out_5(SE), .out_6(SF), .out_7(SG), .out_8(SH), .out_9(SI));  // open: out_0, out_10, out_11, out_12, out_13, out_14, out_15
  assign B = CFB ? CSB : 16'bz;  // Driver driver_23
  assign E = CFE ? CSE : 16'bz;  // Driver driver_24
  assign H = CFH ? CSH : 16'bz;  // Driver driver_25
  PullDown #(.Bits(16)) pulldown_39 (.out(B));
  PullDown #(.Bits(16)) pulldown_40 (.out(E));
  PullDown #(.Bits(16)) pulldown_41 (.out(H));
  assign CBC = not_8_out ? BC : 1'bz;  // Driver driver_26
  assign CBF = not_9_out ? BF : 1'bz;  // Driver driver_27
  assign CBI = not_10_out ? BI : 1'bz;  // Driver driver_28
  not not_8 (not_8_out, delay_50_out);
  Delay #(.delayTime(2)) delay_44 (.in(CBC), .out(delay_44_out));
  Delay #(.delayTime(5)) delay_45 (.in(CLA), .out(delay_45_out));
  not not_9 (not_9_out, delay_51_out);
  Delay #(.delayTime(2)) delay_46 (.in(CBF), .out(delay_46_out));
  Delay #(.delayTime(5)) delay_47 (.in(CLA), .out(delay_47_out));
  not not_10 (not_10_out, delay_52_out);
  Delay #(.delayTime(2)) delay_48 (.in(CBI), .out(delay_48_out));
  Delay #(.delayTime(5)) delay_49 (.in(CLA), .out(delay_49_out));
  D_FF_AS d_ff_as_13 (.Set(1'b0), .D(1'b1), .C(BC), .Clr(CLA), .Q(CFC));  // open: nQ
  PullDown pulldown_42 (.out(CLA));
  D_FF_AS #(.Bits(16)) d_ff_as_14 (.Set(1'b0), .D(SC), .C(delay_44_out), .Clr(delay_45_out), .Q(CSC));  // open: nQ
  PullDown pulldown_43 (.out(delay_45_out));
  D_FF_AS d_ff_as_15 (.Set(1'b0), .D(1'b1), .C(BF), .Clr(CLA), .Q(CFF));  // open: nQ
  PullDown pulldown_44 (.out(CLA));
  D_FF_AS #(.Bits(16)) d_ff_as_16 (.Set(1'b0), .D(SF), .C(delay_46_out), .Clr(delay_47_out), .Q(CSF));  // open: nQ
  PullDown pulldown_45 (.out(delay_47_out));
  D_FF_AS d_ff_as_17 (.Set(1'b0), .D(1'b1), .C(BI), .Clr(CLA), .Q(CFI));  // open: nQ
  PullDown pulldown_46 (.out(CLA));
  D_FF_AS #(.Bits(16)) d_ff_as_18 (.Set(1'b0), .D(SI), .C(delay_48_out), .Clr(delay_49_out), .Q(CSI));  // open: nQ
  PullDown pulldown_47 (.out(delay_49_out));
  Delay delay_50 (.in(CFC), .out(delay_50_out));
  assign C = CFC ? CSC : 16'bz;  // Driver driver_29
  Delay delay_51 (.in(CFF), .out(delay_51_out));
  assign F = CFF ? CSF : 16'bz;  // Driver driver_30
  Delay delay_52 (.in(CFI), .out(delay_52_out));
  assign I = CFI ? CSI : 16'bz;  // Driver driver_31
  PullDown #(.Bits(16)) pulldown_48 (.out(C));
  PullDown #(.Bits(16)) pulldown_49 (.out(F));
  PullDown #(.Bits(16)) pulldown_50 (.out(I));
  SixteenSeg sixteenseg_1 (.led(A), .dp(1'b0));
  SixteenSeg sixteenseg_2 (.led(D), .dp(1'b0));
  SixteenSeg sixteenseg_3 (.led(G), .dp(1'b0));
  SixteenSeg sixteenseg_4 (.led(B), .dp(1'b0));
  SixteenSeg sixteenseg_5 (.led(E), .dp(1'b0));
  SixteenSeg sixteenseg_6 (.led(H), .dp(1'b0));
  SixteenSeg sixteenseg_7 (.led(C), .dp(1'b0));
  SixteenSeg sixteenseg_8 (.led(F), .dp(1'b0));
  SixteenSeg sixteenseg_9 (.led(I), .dp(1'b0));
  Button button_1 (.out(BA));
  Button button_2 (.out(BD));
  Button button_3 (.out(BG));
  Button button_4 (.out(BB));
  Button button_5 (.out(BE));
  Button button_6 (.out(BH));
  Button button_7 (.out(BC));
  Button button_8 (.out(BF));
  Button button_9 (.out(BI));

  assign out_2 = clk;

  // Other names for the same wires on the sheet: CLB = CLA; CLC = CLA; CLD = CLA; CLE = CLA; CLF = CLA; CLG = CLA;
  //   CLH = CLA; CLI = CLA

  // Notes on the sheet:
  //   contents of lookuptable_1 (hex, n*v repeats v):
  //   1,6*0,1
  //   contents of lookuptable_2 (hex, n*v repeats v):
  //   1,6*0,1
  //   contents of lookuptable_3 (hex, n*v repeats v):
  //   1,6*0,1
  //   contents of lookuptable_4 (hex, n*v repeats v):
  //   1,6*0,1
  //   contents of lookuptable_5 (hex, n*v repeats v):
  //   1,6*0,1
  //   contents of lookuptable_6 (hex, n*v repeats v):
  //   1,6*0,1
  //   contents of lookuptable_7 (hex, n*v repeats v):
  //   1,6*0,1
  //   contents of lookuptable_8 (hex, n*v repeats v):
  //   1,6*0,1
endmodule
